# Fritzing sketch sensor_unit_AR_USB_T (saved by Fritzing 0.8.5b)
breadboards: 1

parts:
  Part1 = Arduino Uno (Rev3)
  RHT1 = Humidity and Temperature Sensor RHT03
  R1 = Resistor [tolerance=±5% resistance=1k package=THT]

nets:
  N1: Part1.5V, R1.Pin_1
  N2: RHT1.Data-signal, R1.Pin_0
